# Fritzing sketch Circuit (saved by Fritzing 0.9.4)

parts:
  Mod1 = ESP32 - CAM
  S1 = Toggle Switch [package=THT]
  L298N1 = L298N DC motor driver
  SERVO1 = Tower Pro SG90 servo [part_number=101246]
  M1 = DC Motor  # not connected
  M2 = DC Motor  # not connected

nets:
  5V: Mod1.5V, L298N1.5V
  N1: Mod1.IO12, L298N1.IN1
  N2: Mod1.IO13, L298N1.IN2
  N3: Mod1.IO15, L298N1.IN3
  N4: Mod1.IO14, L298N1.IN4
  N5: Mod1.IO2, SERVO1.Signal
  N6: S1.COM, L298N1.12V

custom parts:
  ESP32 - CAM: The ESP32-CAM has a very competitive small-size camera module that can operate independently as a minimum system with a footprint of only 27*40.5*4.5mm and a deep sleep current of up to 6mA.
  L298N DC motor driver: 2x DC motor driver with 78M05 positive voltage regulator (7..35 V) L298N: max 46 V, 2 A Set 5 V Enable jumper to enable 5 V regultor (needed for the L298N) and +5 V output at screw terminal or supply external +5 V at screw terminal Set ENA and/or ENB to +5 V to enable motor permanently or supply ENA and/or ENB with PWM signal IN1 and IN2 set rotation directory for motor A (OUT1/OUT2) IN2 and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
  Tower Pro SG90 servo: Original file by John De Cristofaro http://www.adafruit.com/products/1449 Adafruit Feedback Servo (Small) Edited by: e-radionica.com 28/9/2015
